# Fritzing sketch fritz11 (saved by Fritzing 0.9.4)

parts:
  Part1 = Arduino Uno (Rev3)
  HC-SR04_Sensor_1 = HC-SR04 Ultrasonic Distance Sensor
  HC-SR04_Sensor_2 = HC-SR04 Ultrasonic Distance Sensor
  HC-SR04_Sensor_3 = HC-SR04 Ultrasonic Distance Sensor
  Part2 = Motor Driver 1A Dual TB6612FNG
  J1 = Basic Servo  # not connected
  M1 = DC Motor
  BAT1 = Battery Holders [package=lipo-1100mAh]
  Part4 = Adafruit BNO055 STEMMA QT [part_number="Adafruit #4646"]
  S1 = Momentary Switch [package=ksa_sealed_tac_switch]
  U1 = SWITCH_SPDT [package=kps-1290]

nets:
  N1: Part1.A0, HC-SR04_Sensor_1.TRIG
  N2: Part1.A1, HC-SR04_Sensor_1.ECHO
  N3: Part1.A2, HC-SR04_Sensor_2.ECHO
  N4: Part1.A3, HC-SR04_Sensor_2.TRIG
  N5: Part1.A4/SDA, Part4.SDA
  N6: Part1.A5/SCL, Part4.SCL
  N7: Part1.D8, HC-SR04_Sensor_3.ECHO
  N8: Part1.D9_PWM, S1.3
  GND: Part1.GND, HC-SR04_Sensor_1.GND, HC-SR04_Sensor_2.GND, HC-SR04_Sensor_3.GND, Part2.GND, Part4.GND, S1.4
  N9: Part1.D3_PWM, Part2.STBY
  N10: Part1.D4, Part2.AIN1
  N11: Part1.D5_PWM, Part2.AIN2
  N12: Part1.D6_PWM, Part2.PWMA
  N13: Part1.D7, HC-SR04_Sensor_3.TRIG
  3V3: Part1.3V3, Part4.3.3V
  VCC: Part1.5V, HC-SR04_Sensor_1.VCC, HC-SR04_Sensor_2.VCC, HC-SR04_Sensor_3.VCC, Part2.VCC, U1.P
  N14: Part1.VIN, BAT1.-
  N15: Part2.A02, M1.pin_1
  N16: Part2.A01, M1.pin_2
  N17: BAT1.+, U1.S

notes:
  [writour note here]

custom parts:
  Adafruit BNO055 STEMMA QT: If you've ever ordered and wire up a 9-DOF sensor, chances are you've also realized the challenge of turning the sensor data from an accelerometer, gyroscope, and magnetometer into actual "3D space orientation"! Orientation is a hard problem to solve. The sensor fusion algorithms (the secret sauce that blends accelerometer, magnetometer, and gyroscope data into stable three-axis orientation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

// code stored in the sketch: Untitled.ino
#include <Pixy2.h>
int x,y,width,height,sign;
#include <Servo.h>
Servo myservo;
Pixy2 pixy;

const int trigPin=3;
const int echoPin=2;

const int m2=9;
const int m1=4;
const int m4=6;
const int m3=11;
long duration;
int distance;
int angle;
const int pwm=10;

void setup() {
  // put your setup code here, to run once:
   pinMode(pwm,OUTPUT);
  pinMode(m1,OUTPUT);
  pinMode(m2,OUTPUT);
  pinMode(m3,OUTPUT);
  pinMode(m4,OUTPUT);
   pinMode(trigPin,OUTPUT);
  pinMode(echoPin,INPUT);

   myservo.attach(7);


  Serial.begin(9600);
  pixy.init();
}

void forward(){
  analogWrite(m1, 200);
   analogWrite(m2, 0);
    analogWrite(m3, 200);
   analogWrite(m4, 0);
  
}
void right(){
  analogWrite(m1,200);
  analogWrite(m2,0);
  analogWrite(m3,0);
  analogWrite(m4,200);
}
void stopp(){
  analogWrite(m1,0);
  analogWrite(m2,0);
  analogWrite(m3,0);
  analogWrite(m4,0);
}
void left(){
  analogWrite(m1,0);
  analogWrite(m2,200);
  analogWrite(m3,200);
  analogWrite(m4,0);
}

void loop() {
  int blockCount = pixy.ccc.getBlocks();

  

  // Process the detected blocks
  if (blockCount > 0) {
    // Retrieve information about the first block
    Block block = pixy.ccc.blocks[0];
     x = block.m_x;        // X coordinate of the block
     y = block.m_y;        // Y coordinate of the block
     width = block.m_width;  // Width of the block
     height = block.m_height; // Height of the block
     sign=block.m_signature;

      Serial.print("X: ");
    Serial.println(x);
    Serial.print("Y: ");
    Serial.println(y);
    Serial.print("Width: ");
    Serial.println(width);
    Serial.print("Height: ");
    Serial.println(height);
    Serial.print("Sign:");
    Serial.println(sign);


 
   

    
 
  }
  digitalWrite(trigPin,LOW);
  delayMicroseconds(2);

  digitalWrite(trigPin,HIGH);
  delayMicroseconds(10);
  digitalWrite(trigPin,LOW);
  duration=pulseIn(echoPin,HIGH);
  distance=duration*0.034/2;
  Serial.println(distance);
  
if (distance<=30)
{
  myservo.write(0);
}
else {
  myservo.write(90);
}
  
  }
